# Fritzing sketch BatteryLight (saved by Fritzing 0.9.6b)
circuit board: 10.5637cm x 5.95444cm
breadboards: 1

parts:
  Attiny84 = IC, DIP package, 14 pins [chip_label=ATtiny84]
  Bat = prefix0000 [form="♂ (male)"]
  IRL_540N1 = Basic FET N-Channel [package="TO220 [THT]"]
  R1 = Resistor [tolerance=±5% power=0.25 resistance=1M package=THT]
  Out- = male pin header, 1 pin [form="♂ (male)"]  # not connected
  Out+ = male pin header, 1 pin [form="♂ (male)"]
  In+ = male pin header, 1 pin [form="♂ (male)"]
  In- = male pin header, 1 pin [form="♂ (male)"]
  In+_2 = male pin header, 1 pin [form="♂ (male)"]
  LED_In- = male pin header, 1 pin [form="♂ (male)"]  # not connected
  Out+_2 = male pin header, 1 pin [form="♂ (male)"]  # not connected
  LED_Out- = male pin header, 1 pin [form="♂ (male)"]  # not connected
  PWM+ = male pin header, 1 pin [form="♂ (male)"]
  PWM- = male pin header, 1 pin [form="♂ (male)"]

nets:
  N1: Attiny84.pin1, Bat.connector0, R1.Pin_0, In+.pin1
  N2: Attiny84.pin6, PWM+.pin1
  N3: Attiny84.pin10, IRL_540N1.gate
  N4: Attiny84.pin14, Bat.connector1, IRL_540N1.source
  N5: IRL_540N1.drain, R1.Pin_1, In-.pin1, PWM-.pin1
  N6: Out+.pin1, In+_2.pin1

notes:
  VCC
  MT3608
  LED source
