# Fritzing sketch RabbitHutchDoorPV (saved by Fritzing 0.9.6b)
circuit board: 9.99091cm x 4.3287cm
breadboards: 1

parts:
  Servo = male pin header, 3 pins [form="♂ (male)"]
  Bat+ = screw terminal, 2 pins
  Buttons = male pin header, 6 pins [form="♂ (male)"]
  IRL_540N = Basic FET N-Channel [package="TO220 [THT]"]
  DHT_22 = Humidity and Temperature Sensor RHT03
  10k = Resistor [tolerance=±5% resistance=10k power=0.25 package=THT]
  WeMos_D1_Mini1_pro = WeMos D1 Mini
  1M = Resistor [tolerance=±5% resistance=1M power=0.25 package=THT]
  10k_2 = Resistor [tolerance=±5% power=0.25 resistance=10k package=THT]
  Cservo = Ceramic Capacitor [capacitance=1µF voltage=35V package="200 mil [THT, multilayer]"]
  1M_2 = Resistor [tolerance=±5% power=0.25 resistance=1M package=THT]
  1M_3 = Resistor [tolerance=±5% power=0.25 resistance=1M package=THT]
  Cclose = Ceramic Capacitor [capacitance=10µF voltage=35V package="200 mil [THT, multilayer]"]
  Copen = Ceramic Capacitor [capacitance=10µF voltage=35V package="200 mil [THT, multilayer]"]
  470 = Resistor [tolerance=±5% power=0.25 resistance=470 package=THT]
  Cvdd = Ceramic Capacitor [capacitance=1µF voltage=35V package="100 mil [THT, multilayer]"]
  Bat+_2 = male pin header, 1 pin [form="♂ (male)"]
  Bat- = male pin header, 1 pin [form="♂ (male)"]
  PV+ = screw terminal, 2 pins
  Out+ = male pin header, 1 pin [form="♂ (male)"]
  Out- = male pin header, 1 pin [form="♂ (male)"]
  PV- = male pin header, 1 pin [form="♂ (male)"]
  PV+_2 = male pin header, 1 pin [form="♂ (male)"]
  Out-_2 = male pin header, 1 pin [form="♂ (male)"]
  Out+_2 = male pin header, 1 pin [form="♂ (male)"]
  In- = male pin header, 1 pin [form="♂ (male)"]
  In+ = male pin header, 1 pin [form="♂ (male)"]

nets:
  N1: Servo.pin1, WeMos_D1_Mini1_pro.D2
  N2: Servo.pin2, Cservo.1, Out+_2.pin1
  N3: Servo.pin3, IRL_540N.drain, DHT_22.GND_1, DHT_22.GND_2, Cservo.0
  N4: Bat+.pin1, Bat+_2.pin1
  N5: Bat+.pin2, Bat-.pin1
  N6: Buttons.pin1, Buttons.pin3, Buttons.pin5, IRL_540N.source, WeMos_D1_Mini1_pro.G, 10k_2.Pin_0, Cclose.1, Copen.1, Cvdd.0, Out-.pin1, Out-_2.pin1, In-.pin1
  N7: Buttons.pin2, WeMos_D1_Mini1_pro.D6, 1M_3.Pin_0, Cclose.0
  N8: Buttons.pin4, WeMos_D1_Mini1_pro.D1, 1M_2.Pin_1, Copen.0
  N9: Buttons.pin6, WeMos_D1_Mini1_pro.RST, 470.Pin_1
  N10: IRL_540N.gate, WeMos_D1_Mini1_pro.D5, 10k_2.Pin_1
  VCC: DHT_22.Vcc, 10k.Pin_1, WeMos_D1_Mini1_pro.3V3, 1M_2.Pin_0, 1M_3.Pin_1, Cvdd.1
  N11: DHT_22.Data-signal, 10k.Pin_0, WeMos_D1_Mini1_pro.D7
  N12: WeMos_D1_Mini1_pro.5V, 1M.Pin_0, Out+.pin1, In+.pin1
  N13: WeMos_D1_Mini1_pro.A0, 1M.Pin_1
  N14: WeMos_D1_Mini1_pro.D0, 470.Pin_0
  N15: PV+.pin1, PV+_2.pin1
  N16: PV+.pin2, PV-.pin1

notes:
  5V
  GND
  open
  close
  reset
  rst
