# Fritzing sketch RemoteControl (saved by Fritzing 0.9.4)
circuit board: 5.0027cm x 4.00456cm
breadboards: 1

parts:
  nRF24L01 = NRF24L01+ Breakout Board
  ATtiny85 = attiny85 [package=dip]
  IRL540N = MOSFET-NCHANNEL [package=to220v]
  in = screw terminal, 2 pins
  out = screw terminal, 3 pins
  MCP1700-330 = NPN-Transistor [package="TO92 [THT]"]
  1uF = Ceramic Capacitor [capacitance=1µF package="100 mil [THT, multilayer]"]
  1uF_2 = Ceramic Capacitor [capacitance=1µF package="100 mil [THT, multilayer]"]
  Power = LED - 3mm [color="Red (633nm)" package="3 mm [THT]"]
  J1 = female pin header, 3 pins [form="♀ (female)"]
  R_LED = Resistor [tolerance=±5% resistance=220 package=THT]

nets:
  N1: nRF24L01.GND, IRL540N.S, in.pin1, MCP1700-330.E, 1uF.0, 1uF_2.0
  N2: nRF24L01.VCC, ATtiny85.Pin_8, out.pin2, MCP1700-330.B, 1uF.1, Power.anode
  N3: nRF24L01.CE, ATtiny85.Pin_5
  N4: nRF24L01.CS, ATtiny85.Pin_7
  N5: nRF24L01.SCK, ATtiny85.Pin_2
  N6: nRF24L01.MOSI, ATtiny85.Pin_6, J1.pin3
  N7: nRF24L01.MISO, ATtiny85.Pin_3
  N8: ATtiny85.Pin_1, J1.pin1
  N9: ATtiny85.Pin_4, IRL540N.D, out.pin1, R_LED.Pin_0
  N10: IRL540N.G, J1.pin2
  N11: in.pin2, out.pin3, MCP1700-330.C, 1uF_2.1
  N12: Power.cathode, R_LED.Pin_1

notes:
  5V
  3V3
