# Fritzing sketch BatteryLight (saved by Fritzing 1.0.1rc)
circuit board: 9.3cm x 5.3cm
breadboards: 1

parts:
  Attiny84 = IC, DIP package, 14 pins [chip_label=ATtiny84]
  Bat = prefix0000 [form="♂ (male)"]
  IRL_540N = Basic FET N-Channel [package="TO220 [THT]"]
  R1 = Resistor [tolerance=±5% power=0.25 resistance=1M package=THT]
  Out- = male pin header, 1 pin [form="♂ (male)"]
  Out+ = male pin header, 1 pin [form="♂ (male)"]
  In+ = male pin header, 1 pin [form="♂ (male)"]
  In- = male pin header, 1 pin [form="♂ (male)"]
  In+_2 = male pin header, 1 pin [form="♂ (male)"]
  LED_In- = male pin header, 1 pin [form="♂ (male)"]
  Out+_2 = male pin header, 1 pin [form="♂ (male)"]
  Out-_2 = male pin header, 1 pin [form="♂ (male)"]
  PWM+ = male pin header, 1 pin [form="♂ (male)"]
  PWM- = male pin header, 1 pin [form="♂ (male)"]
  MCP1700 = Voltage Regulator [package=to-92]
  1uF = Ceramic Capacitor [capacitance=1µF voltage=35V package="200 mil [THT, multilayer]"]
  1uF_2 = Ceramic Capacitor [capacitance=1µF voltage=35V package="200 mil [THT, multilayer]"]
  NRF24LO1 = NRF24L01+ Breakout Board
  100k = Resistor [tolerance=±5% power=0.25 resistance=100k package=THT]
  R4 = Resistor [tolerance=±5% power=0.25 resistance=470k package=THT]
  AM312 = male pin header, 3 pins [form="♂ (male)"]
  BH1750 = male pin header, 4 pins [form="♂ (male)"]
  LED = prefix0000 [form="♂ (male)"]

nets:
  N1: Attiny84.pin1, Bat.connector0, R1.Pin_0, In+.pin1, MCP1700.IN, 1uF_2.1, R4.Pin_0
  N2: Attiny84.pin2, AM312.pin3
  N3: Attiny84.pin3, NRF24LO1.CE
  N4: Attiny84.pin5, NRF24LO1.CS
  N5: Attiny84.pin6, PWM+.pin1
  N6: Attiny84.pin7, NRF24LO1.MISO
  N7: Attiny84.pin8, NRF24LO1.MOSI
  N8: Attiny84.pin9, NRF24LO1.SCK
  N9: Attiny84.pin10, IRL_540N.gate
  N10: Attiny84.pin11, BH1750.pin4
  N11: Attiny84.pin12, BH1750.pin3
  N12: Attiny84.pin13, 100k.Pin_0, R4.Pin_1
  N13: Attiny84.pin14, Bat.connector1, IRL_540N.source, 1uF.0, 1uF_2.0, 100k.Pin_1, AM312.pin2, BH1750.pin2
  N14: IRL_540N.drain, R1.Pin_1, Out-.pin1, In-.pin1, LED_In-.pin1, PWM-.pin1
  N15: Out+.pin1, In+_2.pin1
  N16: Out+_2.pin1, LED.connector0
  N17: Out-_2.pin1, LED.connector1
  GND: MCP1700.GND, NRF24LO1.GND
  N18: MCP1700.OUT, 1uF.1, NRF24LO1.VCC, AM312.pin1, BH1750.pin1

notes:
  VCC
  MT3608
  LED source
  Battery Light V1.0
  +
  Battery Light, 1.0
