# Fritzing sketch BatteryLight (saved by Fritzing 1.0.1rc)
circuit board: 9cm x 5.5cm
breadboards: 1

parts:
  IRL_540N = Basic FET N-Channel [package="TO220 [THT]"]
  1M = Resistor [tolerance=±5% power=0.25 resistance=1M package=THT]
  Out- = male pin header, 1 pin [form="♂ (male)"]
  Out+ = male pin header, 1 pin [form="♂ (male)"]
  In+ = male pin header, 1 pin [form="♂ (male)"]
  In- = male pin header, 1 pin [form="♂ (male)"]
  In+_2 = male pin header, 1 pin [form="♂ (male)"]
  In-_2 = male pin header, 1 pin [form="♂ (male)"]
  Out+_2 = male pin header, 1 pin [form="♂ (male)"]
  Out-_2 = male pin header, 1 pin [form="♂ (male)"]
  PWM+ = male pin header, 1 pin [form="♂ (male)"]
  PWM- = male pin header, 1 pin [form="♂ (male)"]
  MCP1700 = Voltage Regulator [package=to-92]
  1uF = Ceramic Capacitor [capacitance=1µF voltage=35V package="200 mil [THT, multilayer]"]
  1uF_2 = Ceramic Capacitor [capacitance=1µF voltage=35V package="200 mil [THT, multilayer]"]
  NRF24LO1 = NRF24L01+ Breakout Board
  100k = Resistor [tolerance=±5% power=0.25 resistance=100k package=THT]
  470k = Resistor [tolerance=±5% power=0.25 resistance=470k package=THT]
  AM312_1 = male pin header, 3 pins [form="♂ (male)"]
  BH1750 = male pin header, 4 pins [form="♂ (male)"]
  Attiny84 = IC, DIP package, 14 pins [chip_label=ATtiny84]
  Bat = male pin header, 2 pins [form="♂ (male)"]
  LED- = male pin header, 2 pins [form="♂ (male)"]
  AM312_2 = male pin header, 3 pins [form="♂ (male)"]
  In-_3 = male pin header, 1 pin [form="♂ (male)"]  # not connected
  In+_3 = male pin header, 1 pin [form="♂ (male)"]  # not connected
  Out-_3 = male pin header, 1 pin [form="♂ (male)"]
  Bat- = male pin header, 1 pin [form="♂ (male)"]
  Bat+ = male pin header, 1 pin [form="♂ (male)"]
  Out+_3 = male pin header, 1 pin [form="♂ (male)"]
  AM312_1* = male pin header, 3 pins [form="♂ (male)"]
  1uF_3 = Ceramic Capacitor [capacitance=1µF voltage=35V package="200 mil [THT, multilayer]"]

nets:
  N1: IRL_540N.gate, Attiny84.pin10
  N2: IRL_540N.drain, 1M.Pin_1, Out-.pin1, In-.pin1, In-_2.pin1, PWM-.pin1
  GND: IRL_540N.source, 1M.Pin_0, MCP1700.GND, 1uF.0, 1uF_2.0, NRF24LO1.GND, 100k.Pin_1, AM312_1.pin2, BH1750.pin2, Attiny84.pin14, AM312_2.pin2, Out-_3.pin1, AM312_1*.pin2, 1uF_3.1
  N3: Out+.pin1, In+_2.pin1
  N4: In+.pin1, MCP1700.IN, 1uF_2.1, Attiny84.pin1, Out+_3.pin1
  N5: Out+_2.pin1, LED-.pin1
  N6: Out-_2.pin1, LED-.pin2
  N7: PWM+.pin1, Attiny84.pin6
  N8: MCP1700.OUT, 1uF.1, NRF24LO1.VCC, AM312_1.pin1, BH1750.pin1, AM312_2.pin1, AM312_1*.pin1, 1uF_3.0
  N9: NRF24LO1.CE, Attiny84.pin3
  N10: NRF24LO1.CS, Attiny84.pin5
  N11: NRF24LO1.SCK, Attiny84.pin9
  N12: NRF24LO1.MOSI, Attiny84.pin8
  N13: NRF24LO1.MISO, Attiny84.pin7
  N14: 100k.Pin_0, 470k.Pin_1, Attiny84.pin13
  N15: 470k.Pin_0, Bat.pin1, Bat+.pin1
  N16: AM312_1.pin3, Attiny84.pin2, AM312_1*.pin3
  N17: BH1750.pin3, Attiny84.pin12
  N18: BH1750.pin4, Attiny84.pin11
  N19: Attiny84.pin4, AM312_2.pin3
  N20: Bat.pin2, Bat-.pin1

notes:
  VCC
  MT3608
  LED source
  Battery Light V1.1
  +
  Battery Light, 1.0
