# Fritzing sketch D1nRF24LO1 (saved by Fritzing 0.9.6b)
circuit board: 3.86378cm x 7.49956cm
breadboards: 1

parts:
  WeMos_D1_Mini1 = WeMos D1 Mini
  NRF24LO1 = NRF24L01+ Breakout Board
  5V = screw terminal, 2 pins
  3V3 = screw terminal, 2 pins
  SDA = screw terminal, 2 pins
  470 = Resistor [tolerance=±5% power=0.25 resistance=470 package=THT]
  C3v3 = Ceramic Capacitor [capacitance=10µF voltage=35V package="200 mil [THT, multilayer]"]
  BME680 = male pin header, 6 pins [form="♂ (male)"]

nets:
  3V3: WeMos_D1_Mini1.3V3, NRF24LO1.VCC, 3V3.pin1, C3v3.1, BME680.pin6
  N1: WeMos_D1_Mini1.5V, 5V.pin1
  N2: WeMos_D1_Mini1.D0, 470.Pin_1
  N3: WeMos_D1_Mini1.D1, SDA.pin2, BME680.pin4
  N4: WeMos_D1_Mini1.D2, SDA.pin1, BME680.pin3
  N5: WeMos_D1_Mini1.D3, NRF24LO1.CS
  N6: WeMos_D1_Mini1.D5, NRF24LO1.SCK
  N7: WeMos_D1_Mini1.D6, NRF24LO1.MISO
  N8: WeMos_D1_Mini1.D7, NRF24LO1.MOSI
  N9: WeMos_D1_Mini1.D8, NRF24LO1.CE
  N10: WeMos_D1_Mini1.G, NRF24LO1.GND, 5V.pin2, 3V3.pin2, C3v3.0, BME680.pin5
  N11: WeMos_D1_Mini1.RST, 470.Pin_0
