# Fritzing sketch LedStrip (saved by Fritzing 1.0.1rc)
circuit board: 7.5cm x 5.3cm
breadboards: 1

parts:
  Out+ = male pin header, 1 pin [form="♂ (male)"]
  Out- = male pin header, 1 pin [form="♂ (male)"]
  In- = male pin header, 1 pin [form="♂ (male)"]
  In+ = male pin header, 1 pin [form="♂ (male)"]
  MCP1700 = Voltage Regulator [package=to-92]
  1uF = Ceramic Capacitor [capacitance=1µF voltage=35V package="200 mil [THT, multilayer]"]
  1uF_2 = Ceramic Capacitor [capacitance=1µF voltage=35V package="200 mil [THT, multilayer]"]
  100k = Resistor [tolerance=±5% power=0.25 resistance=100k package=THT]
  470k = Resistor [tolerance=±5% power=0.25 resistance=470k package=THT]
  Attiny84 = IC, DIP package, 14 pins [chip_label=ATtiny84]
  Bat = male pin header, 2 pins [form="♂ (male)"]
  Bat+ = male pin header, 1 pin [form="♂ (male)"]
  J1 = male pin header, 1 pin [form="♂ (male)"]  # not connected
  Bat- = male pin header, 1 pin [form="♂ (male)"]
  Out-_2 = male pin header, 1 pin [form="♂ (male)"]
  Out+_2 = male pin header, 1 pin [form="♂ (male)"]
  J2 = male pin header, 1 pin [form="♂ (male)"]  # not connected
  IRL_540N = Basic FET N-Channel [package="TO220 [THT]"]
  1M = Resistor [tolerance=±5% power=0.25 resistance=1M package=THT]
  power = LED - 3mm [color="Red (633nm)" current=0.030 package="3 mm [THT]"]
  AM312 = male pin header, 3 pins [form="♂ (male)"]
  BH1751 = male pin header, 4 pins [form="♂ (male)"]
  10uF = Ceramic Capacitor [capacitance=10µF voltage=35V package="200 mil [THT, multilayer]"]
  100 = Resistor [tolerance=±5% power=0.25 resistance=100 package=THT]
  LED_1 = female pin header, 3 pins [form="♀ (female)"]
  LED_2 = female pin header, 3 pins [form="♀ (female)"]
  on = female pin header, 3 pins [form="♀ (female)"]
  NRF24LO1 = NRF24L01+ Breakout Board
  4k7 = Resistor [tolerance=±5% power=0.25 resistance=4.7k package=THT]

nets:
  N1: Out+.pin1, LED_1.pin1, LED_2.pin1, 4k7.Pin_0
  N2: Out-.pin1, In-.pin1, IRL_540N.drain, 1M.Pin_1, LED_1.pin2, LED_2.pin2, 4k7.Pin_1
  N3: In+.pin1, MCP1700.IN, 1uF_2.1, 470k.Pin_0, Attiny84.pin1, Out+_2.pin1, power.anode
  GND: MCP1700.GND, 1uF.0, 1uF_2.0, 100k.Pin_1, Attiny84.pin14, Out-_2.pin1, IRL_540N.source, 1M.Pin_0, AM312.pin2, BH1751.pin2, 10uF.0, NRF24LO1.GND
  N4: MCP1700.OUT, 1uF.1, AM312.pin1, BH1751.pin1, 10uF.1, NRF24LO1.VCC
  N5: 100k.Pin_0, 470k.Pin_1, Attiny84.pin13
  N6: Attiny84.pin2, AM312.pin3
  N7: Attiny84.pin3, NRF24LO1.CE
  N8: Attiny84.pin5, NRF24LO1.CS
  N9: Attiny84.pin6, LED_1.pin3
  N10: Attiny84.pin7, NRF24LO1.MISO
  N11: Attiny84.pin8, NRF24LO1.MOSI
  N12: Attiny84.pin9, NRF24LO1.SCK
  N13: Attiny84.pin10, IRL_540N.gate, LED_2.pin3
  N14: Attiny84.pin11, BH1751.pin4
  N15: Attiny84.pin12, BH1751.pin3
  N16: Bat.pin1, on.pin2
  N17: Bat.pin2, Bat-.pin1, 100.Pin_0
  N18: Bat+.pin1, on.pin1
  N19: power.cathode, 100.Pin_1

notes:
  XL6009
  LED STRIP V1.0
  LED Strip, 1.0
  charger
