# Fritzing sketch MotionSensor (saved by Fritzing 0.9.6b)
circuit board: 5.95648cm x 3.67925cm
breadboards: 1

parts:
  NRF24L01 = NRF24L01+ Breakout Board
  Attiny84 = IC, DIP package, 14 pins [chip_label=ATtiny84]
  BH1750 = IC, SIP package, 5 pins [chip_label=BH1750]
  MCP1700_3v3 = Voltage Regulator [package=to-92]
  C1 = Ceramic Capacitor [capacitance=1µF voltage=35V package="200 mil [THT, multilayer]"]
  C2 = Ceramic Capacitor [capacitance=1µF voltage=35V package="200 mil [THT, multilayer]"]
  AM312-1 = male pin header, 3 pins [form="♂ (male)"]
  R1 = Resistor [tolerance=±5% power=0.25 resistance=470k package=THT]
  R2 = Resistor [tolerance=±5% power=0.25 resistance=100k package=THT]
  AM312-2 = male pin header, 3 pins [form="♂ (male)"]
  Bat = male pin header, 2 pins [form="♂ (male)"]
  AM312-3 = male pin header, 3 pins [form="♂ (male)"]
  BH1750_2 = male pin header, 4 pins [form="♂ (male)"]

nets:
  GND: NRF24L01.GND, Attiny84.pin14, BH1750.pin2, BH1750.pin5, MCP1700_3v3.GND, C1.1, C2.1, AM312-1.pin3, R2.Pin_1, AM312-2.pin3, Bat.pin2, AM312-3.pin3, BH1750_2.pin3
  N1: NRF24L01.VCC, BH1750.pin1, MCP1700_3v3.OUT, C2.0, AM312-1.pin1, AM312-2.pin1, AM312-3.pin1, BH1750_2.pin4
  N2: NRF24L01.CE, Attiny84.pin3
  N3: NRF24L01.CS, Attiny84.pin5
  N4: NRF24L01.SCK, Attiny84.pin9
  N5: NRF24L01.MOSI, Attiny84.pin8
  N6: NRF24L01.MISO, Attiny84.pin7
  N7: Attiny84.pin1, MCP1700_3v3.IN, C1.0, R1.Pin_0, Bat.pin1
  N8: Attiny84.pin2, AM312-1.pin2
  N9: Attiny84.pin4, AM312-2.pin2
  N10: Attiny84.pin10, AM312-3.pin2
  N11: Attiny84.pin11, BH1750.pin4, BH1750_2.pin1
  N12: Attiny84.pin12, BH1750.pin3, BH1750_2.pin2
  N13: Attiny84.pin13, R1.Pin_1, R2.Pin_0

notes:
  VCC
