# Fritzing sketch TemperatureSensor (saved by Fritzing 1.0.1rc)
circuit board: 4.15cm x 3cm
breadboards: 1

parts:
  1uF = Ceramic Capacitor [capacitance=1µF voltage=35V package="200 mil [THT, multilayer]"]
  1uF_2 = Ceramic Capacitor [capacitance=1µF voltage=35V package="200 mil [THT, multilayer]"]
  470k = Resistor [tolerance=±5% power=0.25 resistance=470k package=THT]
  100k = Resistor [tolerance=±5% power=0.25 resistance=100k package=THT]
  3v3 = Voltage Regulator [package=to-92]
  BME280 = BME280
  NRF24L01 = NRF24L01+ Breakout Board
  TP4056 = TP4056 module
  Attiny84 = IC, DIP package, 14 pins [chip_label=ATtiny84]
  1uF1 = Ceramic Capacitor [capacitance=1µF voltage=35V package="200 mil [THT, multilayer]"]
  PV = male pin header, 2 pins [form="♂ (male)"]
  AM312 = male pin header, 3 pins [form="♂ (male)"]
  Bat = male pin header, 2 pins [form="♂ (male)"]
  S1-1 = female pin header, 2 pins [form="♀ (female)"]
  S1-2 = female pin header, 2 pins [form="♀ (female)"]

nets:
  N1: 1uF.0, 100k.Pin_1, 3v3.IN, TP4056.pin6, Attiny84.pin1, 1uF1.0
  GND: 1uF.1, 1uF_2.1, 470k.Pin_0, 3v3.GND, BME280.GND, NRF24L01.GND, TP4056.pin3, Attiny84.pin14, 1uF1.1, AM312.pin2, S1-1.pin2
  VIN: 1uF_2.0, 3v3.OUT, BME280.VIN, NRF24L01.VCC, AM312.pin1
  N2: 470k.Pin_1, 100k.Pin_0, Attiny84.pin13
  N3: BME280.SCL, Attiny84.pin12
  N4: BME280.SDA, Attiny84.pin11
  N5: NRF24L01.CE, Attiny84.pin3
  N6: NRF24L01.CS, Attiny84.pin5
  N7: NRF24L01.SCK, Attiny84.pin9
  N8: NRF24L01.MOSI, Attiny84.pin8
  N9: NRF24L01.MISO, Attiny84.pin7
  N10: TP4056.pin1, PV.pin1
  N11: TP4056.pin2, PV.pin2
  N12: TP4056.pin4, Bat.pin2
  N13: TP4056.pin5, Bat.pin1
  N14: Attiny84.pin2, AM312.pin3
  N15: Attiny84.pin10, S1-2.pin2

notes:
  Temp Sensor V1.1
  nRF24 Temperature Sensor, 1.1

custom parts:
  BME280: Temperature Humidity Barometric presure Sensor
  TP4056 module: Battery Charging Board Micro USB 5V 1A 18650 Lithium Battery Charger Module.
